# Fritzing sketch fritzing (saved by Fritzing 0.9.0b)
breadboards: 1

parts:
  R1 = Resistor [tolerance=±5% resistance=220 package=THT]
  LED1 = LED - 5mm [color="Red (633nm)" package="5 mm [THT]"]
  SPKR1 = Loudspeaker
  Parte1 = Arduino Uno (Rev3)
  S1 = Toggle Switch [package=THT]
  R2 = Resistor [tolerance=±5% resistance=10k package=THT]
  R3 = Resistor [tolerance=±5% resistance=10k package=THT]

nets:
  N1: R1.Pin_1, SPKR1.pin1, Parte1.GND, R2.Pin_1, R3.Pin_1
  N2: LED1.cathode, LED1.anode
  N3: SPKR1.pin2, Parte1.D3_PWM
  N4: Parte1.D8, R2.Pin_0
  N5: Parte1.D4, S1.L2, R3.Pin_0
  N6: Parte1.5V, S1.COM
