# Fritzing sketch fritzing (saved by Fritzing 0.9.0b)
breadboards: 1

parts:
  Parte1 = Arduino Uno (Rev3)
  LED1 = LED - 5mm [color="Red (633nm)" package="5 mm [THT]"]
  LED2 = LED - 5mm [color="Green (570nm)" package="5 mm [THT]"]
  R1 = Resistor [tolerance=±5% resistance=220 package=THT]
  R2 = Resistor [tolerance=±5% resistance=220 package=THT]
  S1 = Pushbutton [package="[THT]"]
  R3 = Resistor [tolerance=±5% resistance=220 package=THT]
  J1 = Basic Servo

nets:
  N1: Parte1.D9_PWM, J1.pulse
  N2: Parte1.D12/MISO, R2.Pin_0
  N3: Parte1.D13/SCK, R1.Pin_0
  N4: Parte1.D2, S1.Pin_3, S1.Pin_4, R3.Pin_1
  5V: Parte1.5V, LED1.anode, LED2.anode, S1.Pin_1, S1.Pin_2, J1.vcc
  GND: Parte1.GND, R3.Pin_0, J1.gnd
  N5: LED1.cathode, R1.Pin_1
  N6: LED2.cathode, R2.Pin_1
