# Fritzing sketch fritzing (saved by Fritzing 0.9.3b)
breadboards: 1

parts:
  hc-sr1 = hc-sr04
  Componente1 = Arduino Uno (Rev3)
  J1 = Basic Servo

nets:
  VCC: hc-sr1.VCC, Componente1.5V, J1.vcc
  N1: hc-sr1.Trig, Componente1.D11_PWM/MOSI
  N2: hc-sr1.Echo, Componente1.D12/MISO
  GND: hc-sr1.GND, Componente1.GND, J1.gnd
  N3: Componente1.D9_PWM, J1.pulse
