# Fritzing sketch fritzing (saved by Fritzing 0.9.3b)
breadboards: 1

parts:
  Arduino1 = Arduino Uno (Rev3)
  LED1 = LED - 5mm [color="Red (633nm)" package="5 mm [THT]"]
  LED2 = LED - 5mm [color="Red (633nm)" package="5 mm [THT]"]
  LED3 = LED - 5mm [color="Red (633nm)" package="5 mm [THT]"]
  LED4 = LED - 5mm [color="Red (633nm)" package="5 mm [THT]"]
  LED5 = LED - 5mm [color="Red (633nm)" package="5 mm [THT]"]
  LED6 = LED - 5mm [color="Red (633nm)" package="5 mm [THT]"]
  R2 = Resistor [tolerance=±5% resistance=220 package=THT]
  R3 = Resistor [tolerance=±5% resistance=220 package=THT]
  R4 = Resistor [tolerance=±5% resistance=220 package=THT]
  R5 = Resistor [tolerance=±5% resistance=220 package=THT]
  R6 = Resistor [tolerance=±5% resistance=220 package=THT]
  R7 = Resistor [tolerance=±5% resistance=220 package=THT]

nets:
  N1: Arduino1.D8, LED6.anode
  N2: Arduino1.D9_PWM, LED5.anode
  N3: Arduino1.D10_PWM/SS, LED4.anode
  N4: Arduino1.D11_PWM/MOSI, LED3.anode
  N5: Arduino1.D12/MISO, LED2.anode
  N6: Arduino1.D13/SCK, LED1.anode
  N7: Arduino1.GND, R2.Pin_1, R3.Pin_1, R4.Pin_1, R5.Pin_1, R6.Pin_1, R7.Pin_1
  N8: LED1.cathode, R2.Pin_0
  N9: LED2.cathode, R3.Pin_0
  N10: LED3.cathode, R4.Pin_0
  N11: LED4.cathode, R5.Pin_0
  N12: LED5.cathode, R6.Pin_0
  N13: LED6.cathode, R7.Pin_0
