# Fritzing sketch fritzing (saved by Fritzing 0.9.0b)
breadboards: 1

parts:
  LED1 = LED - 5mm [color="Red (633nm)" package="5 mm [THT]"]
  LED2 = LED - 5mm [color="Green (570nm)" package="5 mm [THT]"]
  LED3 = LED - 5mm [color="White (4500K)" package="5 mm [THT]"]
  R1 = Resistor [tolerance=±5% resistance=220 package=THT]
  R2 = Resistor [tolerance=±5% resistance=220 package=THT]
  R3 = Resistor [tolerance=±5% resistance=220 package=THT]
  Parte1 = Arduino Uno (Rev3)
  T1 = LM35 Temperature Sensor [package="TO92 [THT]"]
  Q1 = NPN-Transistor [package="TO92 [THT]"]
  LED4 = LED - 5mm [color="Green (570nm)" package="5 mm [THT]"]
  R4 = Resistor [tolerance=±5% resistance=220 package=THT]
  M1 = DC Motor

nets:
  GND: LED1.cathode, LED2.cathode, Parte1.GND, T1.GND, Q1.C, M1.pin_2
  N1: LED1.anode, R1.Pin_0
  N2: LED2.anode, R2.Pin_0
  N3: LED3.anode, R3.Pin_0
  N4: R1.Pin_1, Parte1.D10_PWM/SS
  N5: R2.Pin_1, Parte1.D11_PWM/MOSI
  N6: R3.Pin_1, Parte1.D12/MISO
  N7: Parte1.A0, T1.Vout
  N8: Parte1.D7, LED4.cathode, LED4.anode, R4.Pin_1
  N9: Parte1.5V, T1.+Vs
  N10: Q1.B, R4.Pin_0
