# Fritzing sketch fritzing (saved by Fritzing 0.9.0b)
breadboards: 1

parts:
  Parte1 = Arduino Uno (Rev3)
  Parte2 = Breakout Board for Electret Microphone
  LED1 = LED - 5mm [color="Green (555nm)" package="5 mm [THT]"]
  LED2 = LED - 5mm [color="Yellow (585nm)" package="5 mm [THT]"]
  LED3 = LED - 5mm [color="Red (633nm)" package="5 mm [THT]"]
  R1 = Resistor [tolerance=±5% resistance=220 package=THT]
  R2 = Resistor [tolerance=±5% resistance=1.5k package=THT]
  U1 = Voltage Regulator - 5V [package="DPak [SMD]"]
  U2 = Voltage Regulator - 5V [package="DPak [SMD]"]
  U3 = Voltage Regulator - 5V [package="DPak [SMD]"]
  R4 = Resistor [tolerance=±5% resistance=220 package=THT]  # not connected
  VCC1 = Battery block 9V

nets:
  N1: Parte1.A0, Parte2.AUD
  N2: Parte1.D11_PWM/MOSI, R1.Pin_0
  N3: Parte1.D12/MISO, R2.Pin_0
  5V: Parte1.5V, Parte2.VCC
  GND: Parte1.GND, Parte2.GND
  N4: LED1.cathode, U3.output_voltage
  N5: LED1.anode, LED2.anode, LED3.anode, VCC1.+
  N6: LED2.cathode, U1.GND
  N7: LED3.cathode, U2.GND
  N8: R1.Pin_1, U2.input_voltage
  N9: R2.Pin_1, U1.input_voltage
  N10: U1.output_voltage, U2.output_voltage, U3.GND, VCC1.-
