# Fritzing sketch fritzing (saved by Fritzing 0.9.0b)
breadboards: 1

parts:
  R1 = Resistor [tolerance=±5% resistance=220 package=THT]
  R2 = Resistor [tolerance=±5% resistance=220 package=THT]
  R3 = Resistor [tolerance=±5% resistance=220 package=THT]
  R4 = Resistor [tolerance=±5% resistance=220 package=THT]
  R5 = Resistor [tolerance=±5% resistance=220 package=THT]
  LED1 = LED - 5mm [color="Red (633nm)" package="5 mm [THT]"]
  LED2 = LED - 5mm [color="Orange (620nm)" package="5 mm [THT]"]
  LED3 = LED - 5mm [color="Green (570nm)" package="5 mm [THT]"]
  LED4 = LED - 5mm [color="Red (633nm)" package="5 mm [THT]"]
  LED5 = LED - 5mm [color="Green (570nm)" package="5 mm [THT]"]
  Parte1 = Arduino Uno (Rev3)
  R6 = Resistor [tolerance=±20% resistance=10k package=THT]
  S1 = Pushbutton [package="[THT]"]

nets:
  N1: R1.Pin_0, R2.Pin_0, R3.Pin_0, R4.Pin_0, R5.Pin_0, Parte1.GND, R6.Pin_0
  N2: R1.Pin_1, LED1.cathode
  N3: R2.Pin_1, LED2.cathode
  N4: R3.Pin_1, LED3.cathode
  N5: R4.Pin_1, LED4.cathode
  N6: R5.Pin_1, LED5.cathode
  N7: LED1.anode, Parte1.D13/SCK
  N8: LED2.anode, Parte1.D12/MISO
  N9: LED3.anode, Parte1.D11_PWM/MOSI
  N10: LED4.anode, Parte1.D10_PWM/SS
  N11: LED5.anode, Parte1.D9_PWM
  N12: Parte1.D2, R6.Pin_1, S1.Pin_3, S1.Pin_4
  N13: Parte1.5V, S1.Pin_1, S1.Pin_2
