# Fritzing sketch fritzing (saved by Fritzing 0.9.3b)
breadboards: 1

parts:
  Parte1 = Arduino Uno (Rev3)
  J1 = Piezo Speaker
  LED2 = LED - 5mm [color="Red (633nm)" package="5 mm [THT]"]
  LED3 = LED - 5mm [color="Red (633nm)" package="5 mm [THT]"]
  R2 = Resistor [tolerance=±5% resistance=220 package=THT]
  R3 = Resistor [tolerance=±5% resistance=220 package=THT]
  LED7 = LED - 5mm [color="Orange (612nm)" package="5 mm [THT]"]
  R4 = Resistor [tolerance=±5% resistance=220 package=THT]
  R5 = Resistor [tolerance=±5% resistance=220 package=THT]
  LED8 = LED - 5mm [color="Orange (612nm)" package="5 mm [THT]"]
  LED9 = LED - 5mm [color="White (4500K)" package="5 mm [THT]"]
  R6 = Resistor [tolerance=±5% resistance=220 package=THT]
  LED10 = LED - 5mm [color="White (4500K)" package="5 mm [THT]"]
  R7 = Resistor [tolerance=±5% resistance=220 package=THT]
  hc-sr1 = hc-sr04

nets:
  N1: Parte1.D8, R5.Pin_1
  N2: Parte1.D9_PWM, R2.Pin_1
  N3: Parte1.D10_PWM/SS, R3.Pin_1
  N4: Parte1.D11_PWM/MOSI, J1.pin2
  GND: Parte1.GND, J1.pin1, LED2.cathode, LED3.cathode, LED7.cathode, LED8.cathode, LED9.cathode, LED10.cathode, hc-sr1.GND
  N5: Parte1.D2, hc-sr1.Echo
  N6: Parte1.D3_PWM, hc-sr1.Trig
  N7: Parte1.D5_PWM, R7.Pin_1
  N8: Parte1.D6_PWM, R6.Pin_1
  N9: Parte1.D7, R4.Pin_1
  5V: Parte1.5V, hc-sr1.VCC
  N10: LED2.anode, R3.Pin_0
  N11: LED3.anode, R2.Pin_0
  N12: LED7.anode, R5.Pin_0
  N13: R4.Pin_0, LED8.anode
  N14: LED9.anode, R6.Pin_0
  N15: LED10.anode, R7.Pin_0
