# Fritzing sketch fritzing (saved by Fritzing 0.9.3b)
breadboards: 1

parts:
  Arduino1 = Arduino Uno (Rev3)
  J1 = Basic Servo
  R3 = Trimmer Potentiometer [maximum_resistance=10kΩ package=THT]

nets:
  N1: Arduino1.A0, R3.wiper
  N2: Arduino1.D9_PWM, J1.pulse
  5V: Arduino1.5V, J1.vcc, R3.leg1
  GND: Arduino1.GND, J1.gnd, R3.leg2
