# Fritzing sketch fritzing (saved by Fritzing 0.9.3b)
breadboards: 1

parts:
  J1 = Piezo Speaker
  Componente1 = Arduino Uno (Rev3)
  hc-sr1 = hc-sr04

nets:
  GND: J1.pin1, Componente1.GND, hc-sr1.GND
  N1: J1.pin2, Componente1.D11_PWM/MOSI
  N2: Componente1.D9_PWM, hc-sr1.Echo
  N3: Componente1.D10_PWM/SS, hc-sr1.Trig
  5V: Componente1.5V, hc-sr1.VCC
