# Fritzing sketch fritzing (saved by Fritzing 0.9.3b)
breadboards: 1

parts:
  Componente1 = Arduino Uno (Rev3)
  Componente2 = Thumb Joystick
  R1 = Resistor [tolerance=±5% resistance=220 package=THT]
  LED1 = LED - 5mm [color="Red (633nm)" package="5 mm [THT]"]  # not connected

nets:
  N1: Componente1.A3, Componente2.HORZ
  N2: Componente1.A4/SDA, Componente2.VERT
  GND: Componente1.GND, Componente2.GND, R1.Pin_0
  N3: Componente1.D1/TX, Componente2.VCC
  N4: Componente1.5V, Componente2.SEL
