# Fritzing sketch fritzing (saved by Fritzing 0.9.0b)
breadboards: 1

parts:
  Componente1 = Arduino Uno (Rev3)
  S1 = Momentary Switch [package=ksa_sealed_tac_switch]
  S2 = Momentary Switch [package=ksa_sealed_tac_switch]
  S3 = Momentary Switch [package=ksa_sealed_tac_switch]
  S4 = Momentary Switch [package=ksa_sealed_tac_switch]
  R1 = Resistor [tolerance=±5% resistance=220 package=THT]
  LED1 = LED - 5mm [color="Red (633nm)" package="5 mm [THT]"]
  R2 = Resistor [tolerance=±5% resistance=220 package=THT]
  LED2 = LED - 5mm [color="Green (570nm)" package="5 mm [THT]"]
  R3 = Resistor [tolerance=±5% resistance=220 package=THT]
  LED3 = LED - 5mm [color="Yellow (595nm)" package="5 mm [THT]"]
  R4 = Resistor [tolerance=±5% resistance=220 package=THT]
  LED4 = LED - 5mm [color="Blue (505nm)" package="5 mm [THT]"]
  R5 = Resistor [tolerance=±5% resistance=10k package=THT]
  R6 = Resistor [tolerance=±5% resistance=10k package=THT]
  R7 = Resistor [tolerance=±5% resistance=10k package=THT]
  R8 = Resistor [tolerance=±5% resistance=10k package=THT]

nets:
  N1: Componente1.D10_PWM/SS, LED4.anode
  N2: Componente1.D11_PWM/MOSI, LED3.anode
  N3: Componente1.D12/MISO, R2.Pin_0, LED2.cathode
  N4: Componente1.D13/SCK, LED1.anode
  N5: Componente1.D4, S4.2, R8.Pin_0
  N6: Componente1.D5_PWM, S3.2, R7.Pin_0
  N7: Componente1.D6_PWM, S2.2, R6.Pin_0
  N8: Componente1.D7, S1.2, R5.Pin_0
  N9: S1.4, S2.4, S3.4, S4.4
  N10: R1.Pin_0, LED1.cathode
  N11: R1.Pin_1, R2.Pin_1, R3.Pin_1, R4.Pin_1
  N12: R3.Pin_0, LED3.cathode
  N13: R4.Pin_0, LED4.cathode
  N14: R5.Pin_1, R6.Pin_1, R7.Pin_1, R8.Pin_1
